# Fritzing sketch plant pcb (saved by Fritzing 0.9.3b)
circuit board: 8.46667cm x 5.64444cm
breadboards: 2

parts:
  Part1 = Photon
  R1 = PHOTOCELL [package=photocell]
  R2 = Resistor [tolerance=±5% resistance=220 package="1206 [SMD]"]
  Part2 = Arduino BT
  Part3 = Soil Moisture Sensor
  Part4 = Breakout Board for Electret Microphone
  LED1 = LEDs [package=led10mm]
  LED2 = LEDs [package=led10mm]

nets:
  N1: Part1.A0, Part1.A2, R1.P$1
  N2: Part1.A5, R1.P$2, R2.Pin_0
  N3: Part1.GND, R2.Pin_1, LED2.C
  N4: Part1.D6, LED2.A
  VCC: Part2.5V, Part3.VCC, Part4.VCC
  GND: Part2.GND, Part3.GND, Part4.GND, LED1.C
  N5: Part2.A0, Part3.SIG
  N6: Part2.D2, Part4.AUD
